# Fritzing sketch circuit (saved by Fritzing 0.9.3b)

parts:
  R2 = Resistor [tolerance=±1% resistance=1k package=THT]
  R1 = Resistor [tolerance=±1% resistance=2k package=THT]

nets:
  Onkyo RI Equipment Output (5V): R2.Pin_0
  Raspberry Pi Input (3.3V): R2.Pin_1, R1.Pin_0
  GND: R1.Pin_1
